// Logisim project snake_mark_4.circ as structural Verilog: 22 circuits, main circuit main
module main (
);

  wire clock_1_out, controlled_buffer_1_out, keyboard_1_avail;
  wire [3:0] game_1_digit_0, game_1_digit_1, game_1_digit_2;
  wire [6:0] ASCII;
  wire [31:0] game_1_out_2, game_1_out_3, game_1_out_4, game_1_out_5, game_1_out_6, game_1_out_7,
       game_1_out_8, game_1_out_9, game_1_out_10, game_1_out_11, game_1_out_12, game_1_out_13, game_1_out_14,
       game_1_out_15, game_1_out_16, game_1_out_17, game_1_out_18, game_1_out_19, game_1_out_20,
       game_1_out_21, game_1_out_22, game_1_out_23, game_1_out_24, game_1_out_25, game_1_out_26,
       game_1_out_27, game_1_out_28, game_1_out_29, game_1_out_30, game_1_out_31, game_1_out_32,
       game_1_out_33;

  Hex_Digit_Display hex_digit_display_1 (.value(game_1_digit_2));  // open: dp
  Hex_Digit_Display hex_digit_display_2 (.value(game_1_digit_1));  // open: dp
  Hex_Digit_Display hex_digit_display_3 (.value(game_1_digit_0));  // open: dp
  Clock clock_1 (.out(clock_1_out));
  DotMatrix #(.inputtype("row"), .matrixcols(32), .matrixrows(32)) dotmatrix_1 (
    .row0(game_1_out_2), .row1(game_1_out_6), .row2(game_1_out_10), .row3(game_1_out_14),
    .row4(game_1_out_18), .row5(game_1_out_22), .row6(game_1_out_26), .row7(game_1_out_30),
    .row8(game_1_out_3), .row9(game_1_out_7), .row10(game_1_out_11), .row11(game_1_out_15),
    .row12(game_1_out_19), .row13(game_1_out_23), .row14(game_1_out_27), .row15(game_1_out_31),
    .row16(game_1_out_4), .row17(game_1_out_8), .row18(game_1_out_12), .row19(game_1_out_16),
    .row20(game_1_out_20), .row21(game_1_out_24), .row22(game_1_out_28), .row23(game_1_out_32),
    .row24(game_1_out_5), .row25(game_1_out_9), .row26(game_1_out_13), .row27(game_1_out_17),
    .row28(game_1_out_21), .row29(game_1_out_25), .row30(game_1_out_29), .row31(game_1_out_33));
  game game_1 (
    .ASCII(ASCII), .digit_0(game_1_digit_0), .digit_1(game_1_digit_1), .digit_2(game_1_digit_2),
    .out_2(game_1_out_2), .out_6(game_1_out_6), .out_10(game_1_out_10), .out_14(game_1_out_14),
    .out_18(game_1_out_18), .out_22(game_1_out_22), .out_26(game_1_out_26), .out_30(game_1_out_30),
    .out_3(game_1_out_3), .out_7(game_1_out_7), .out_11(game_1_out_11), .out_15(game_1_out_15),
    .out_19(game_1_out_19), .out_23(game_1_out_23), .out_27(game_1_out_27), .out_31(game_1_out_31),
    .out_4(game_1_out_4), .out_8(game_1_out_8), .out_12(game_1_out_12), .out_16(game_1_out_16),
    .out_20(game_1_out_20), .out_24(game_1_out_24), .out_28(game_1_out_28), .out_32(game_1_out_32),
    .out_5(game_1_out_5), .out_9(game_1_out_9), .out_13(game_1_out_13), .out_17(game_1_out_17),
    .out_21(game_1_out_21), .out_25(game_1_out_25), .out_29(game_1_out_29), .out_33(game_1_out_33));
  assign controlled_buffer_1_out = keyboard_1_avail ? clock_1_out : 1'bz;  // Controlled_Buffer controlled_buffer_1
  Keyboard keyboard_1 (.clk(controlled_buffer_1_out), .avail(keyboard_1_avail), .data(ASCII));  // open: re, clr

  // Notes on the sheet:
  //   Нажать на кнопку
  //   Инструкция
  //   Управление:
  //   w - up
  //   a - left
  //   s - down
  //   d - right
  //   Перед игрой нажать на кнопку под дисплеем
endmodule

module game (
  input  [6:0] ASCII,
  output [31:0] out_2,
  output [31:0] out_3,
  output [31:0] out_4,
  output [31:0] out_5,
  output [31:0] out_6,
  output [31:0] out_7,
  output [31:0] out_8,
  output [31:0] out_9,
  output [31:0] out_10,
  output [31:0] out_11,
  output [31:0] out_12,
  output [31:0] out_13,
  output [31:0] out_14,
  output [31:0] out_15,
  output [31:0] out_16,
  output [31:0] out_17,
  output [31:0] out_18,
  output [31:0] out_19,
  output [31:0] out_20,
  output [31:0] out_21,
  output [31:0] out_22,
  output [31:0] out_23,
  output [31:0] out_24,
  output [31:0] out_25,
  output [31:0] out_26,
  output [31:0] out_27,
  output [31:0] out_28,
  output [31:0] out_29,
  output [31:0] out_30,
  output [31:0] out_31,
  output [31:0] out_32,
  output [31:0] out_33,
  output [3:0] digit_2,
  output [3:0] digit_1,
  output [3:0] digit_0
);

  wire apple_is_eaten, clock_1_out, clock_2_out, clock_3_out, clock_4_out, clock_5_out, down, Err, L,
       movement_1_value, new_apple, not_1_out, or_1_out, R, request_check_crash, snake_crashed, stop, up;
  wire [1:0] direction, scanned_direction;
  wire [2:0] multiplexer_1_out, screen_select;
  wire [3:0] movement_1_x, movement_1_y, x_food, X_head, x_new_head, x_new_tail, X_tail, y_food, Y_head,
       y_new_head, Y_new_tail, Y_tail;
  wire [15:0] data_to_screen_1_out_11, data_to_screen_1_out_12, data_to_screen_1_out_13,
       data_to_screen_1_out_14, data_to_screen_1_out_15, data_to_screen_1_out_16, data_to_screen_1_out_17,
       data_to_screen_1_out_18, data_to_screen_1_out_19, data_to_screen_1_out_20, data_to_screen_1_out_21,
       data_to_screen_1_out_22, data_to_screen_1_out_23, data_to_screen_1_out_24, data_to_screen_1_out_25,
       data_to_screen_1_out_26;

  Clock clock_1 (.out(clock_1_out));
  or or_1 (or_1_out, snake_crashed, stop);
  Clock clock_2 (.out(clock_2_out));
  direction direction_1 (
    .UP(up), .DOWN(down), .Clock(clock_1_out), .LEFT(L), .RIGHT(R), .State(direction),
    .cur_dir(scanned_direction));
  food_generating food_generating_1 (
    .clock(clock_2_out), .new_apple(new_apple), .Err(Err), .food_x(x_food), .food_y(y_food), .stop(stop));
  keyboard_input keyboard_input_1 (.in_1(ASCII), .left(L), .right(R), .up(up), .down(down));
  movement movement_1 (
    .Direction(direction), .X_head(X_head), .Y_head(Y_head), .X_tail(X_tail), .Y_tail(Y_tail),
    .Value(movement_1_value), .X(movement_1_x), .Y(movement_1_y), .new_apple(new_apple), .X_food(x_food),
    .Y_food(y_food), .out_x_head(x_new_head), .out_y_head(y_new_head), .out_x_tail(x_new_tail),
    .out_y_tail(Y_new_tail), .is_eaten(apple_is_eaten), .stop_work_if_1(or_1_out),
    .out_15(scanned_direction), .check_crash_if_1(request_check_crash), .num_of_screen(screen_select));
  score score_1 (.apple_is_eaten(apple_is_eaten), .third_digit(digit_2), .second_digit(digit_1), .first_digit(digit_0));
  Clock clock_3 (.out(clock_3_out));
  Clock clock_4 (.out(clock_4_out));
  coords coords_1 (.X(x_new_head), .Y(y_new_head), .out_4(X_head), .out_5(Y_head), .Clock(clock_3_out));
  Clock clock_5 (.out(clock_5_out));
  Multiplexer #(.width(3)) multiplexer_1 (
    .in0(screen_select), .in1(3'b010), .out(multiplexer_1_out), .sel(snake_crashed));  // open: en
  data_to_screen data_to_screen_1 (
    .clock(clock_4_out), .X(movement_1_x), .Y(movement_1_y), .Value(movement_1_value),
    .out_11(data_to_screen_1_out_11), .out_12(data_to_screen_1_out_12), .out_13(data_to_screen_1_out_13),
    .out_15(data_to_screen_1_out_15), .out_16(data_to_screen_1_out_16), .out_17(data_to_screen_1_out_17),
    .out_18(data_to_screen_1_out_18), .out_19(data_to_screen_1_out_19), .out_20(data_to_screen_1_out_20),
    .out_21(data_to_screen_1_out_21), .out_22(data_to_screen_1_out_22), .out_23(data_to_screen_1_out_23),
    .out_24(data_to_screen_1_out_24), .out_25(data_to_screen_1_out_25), .out_26(data_to_screen_1_out_26),
    .out_14(data_to_screen_1_out_14), .X_FOOD(x_food), .Y_FOOD(y_food), .Err(Err), .Y_Head(Y_head),
    .X_Head(X_head), .request(request_check_crash), .crash(snake_crashed));  // open: Stop
  not not_1 (not_1_out, request_check_crash);
  coords coords_2 (.X(x_new_tail), .Y(Y_new_tail), .out_4(X_tail), .out_5(Y_tail), .Clock(clock_5_out));
  screen_chooser screen_chooser_1 (
    .screen_select(multiplexer_1_out), .in_2(data_to_screen_1_out_11), .in_3(data_to_screen_1_out_12),
    .in_4(data_to_screen_1_out_13), .in_5(data_to_screen_1_out_14), .in_6(data_to_screen_1_out_15),
    .in_7(data_to_screen_1_out_16), .in_8(data_to_screen_1_out_17), .in_9(data_to_screen_1_out_18),
    .in_10(data_to_screen_1_out_19), .in_11(data_to_screen_1_out_20), .in_12(data_to_screen_1_out_21),
    .in_13(data_to_screen_1_out_22), .in_14(data_to_screen_1_out_23), .in_15(data_to_screen_1_out_24),
    .in_16(data_to_screen_1_out_25), .in_17(data_to_screen_1_out_26), .line_1(out_2), .line_2(out_6),
    .line_3(out_10), .line_4(out_14), .line_5(out_18), .line_6(out_22), .line_7(out_26), .line_8(out_30),
    .line_9(out_3), .line_10(out_7), .line_11(out_11), .line_12(out_15), .line_13(out_19), .line_14(out_23),
    .line_15(out_27), .line_16(out_31), .line_17(out_4), .line_18(out_8), .line_19(out_12), .line_20(out_16),
    .line_21(out_20), .line_22(out_24), .line_23(out_28), .line_24(out_32), .line_25(out_5), .line_26(out_9),
    .line_27(out_13), .line_28(out_17), .line_29(out_21), .line_30(out_25), .line_31(out_29), .line_32(out_33));

  // Other names for the same wires on the sheet: _1[31:0] = out_2; _2[31:0] = out_6; _3[31:0] = out_10;
  //   _4[31:0] = out_14; _5[31:0] = out_18; _6[31:0] = out_22; _7[31:0] = out_26; _8[31:0] = out_30; _9[31:0] = out_3;
  //   _10[31:0] = out_7; _11[31:0] = out_11; _12[31:0] = out_15; _13[31:0] = out_19; _14[31:0] = out_23;
  //   _15[31:0] = out_27; _16[31:0] = out_31; _17[31:0] = out_4; _18[31:0] = out_8; _19[31:0] = out_12;
  //   _20[31:0] = out_16; _21[31:0] = out_20; _22[31:0] = out_24; _23[31:0] = out_28; _24[31:0] = out_32;
  //   _25[31:0] = out_5; _26[31:0] = out_9; _27[31:0] = out_13; _28[31:0] = out_17; _29[31:0] = out_21;
  //   _30[31:0] = out_25; _31[31:0] = out_29; _32[31:0] = out_33

  // Notes on the sheet:
  //   Apple coordinates
  //   Work with the keyboard and direction
  //   Movement logic and screen data
  //   Counter
  //   Head
  //   Coordinates
  //   Tail
  //   Screen Output
endmodule

module movement (
  input  [1:0] Direction,
  input  [3:0] X_head,
  input  [3:0] Y_head,
  input  [3:0] X_tail,
  input  [3:0] Y_tail,
  input  [3:0] X_food,
  input  [3:0] Y_food,
  input  stop_work_if_1,
  output check_crash_if_1,
  output new_apple,
  output [3:0] out_x_head,
  output [3:0] X,
  output [2:0] num_of_screen,
  output [3:0] out_y_head,
  output [1:0] out_15,
  output [3:0] out_x_tail,
  output Value,
  output [3:0] Y,
  output [3:0] out_y_tail,
  output is_eaten
);

  wire and_1_out, and_2_out, and_5_out, and_6_out, and_7_out, and_8_out, and_9_out, and_10_out,
       eat_apple_1_is_eat_apple, in_out_prime, IO_sel, move_head, move_tail, n8_to_1_2_out_2, not_1_out,
       not_2_out, not_3_out, not_4_out, not_5_out, not_6_out;
  wire [1:0] n4_to_2_1_out_2, n4_to_2_2_out_2, n4_to_2_3_out_2, n4_to_2_4_out_2, tail_dir_sdv;
  wire [2:0] n8_3_1_out_2;
  wire [3:0] head_dir, IO_adr, n8_to_4_1_out_2, n8_to_4_2_out_2, n8_to_4_3_out_2, n8_to_4_4_out_2,
       n8_to_4_5_out_2, n8_to_4_6_out_2, n8_to_4_7_out_2, n8_to_4_8_out_2, n8_to_4_9_out_2, n8_to_4_10_out_2,
       n8_to_4_11_out_2, n8_to_4_12_out_2, n8_to_4_13_out_2, n8_to_4_14_out_2, n8_to_4_15_out_2, new_apple_t,
       scanned_dir, screen_sel, tail_dir;
  wire [5:0] shifter_4_out;
  wire [7:0] and_11_out, and_12_out, data_line, demultiplexer_1_out9, demultiplexer_1_out10,
       demultiplexer_1_out11, demultiplexer_1_out12, demultiplexer_1_out13, demultiplexer_1_out14,
       demultiplexer_1_out15, dir, head_coords, head_dir_sdv, head_sdvig_5, is_eaten_t,
       module_cdm8_1_io_output, multiplexer_4_out, register_1_q, register_10_q, tail_coords, tail_sdvig_5,
       x_food_t, x_head_t, x_tail_t, y_food_t;
  wire [7:4] y_head_t, y_tail_t;

  // Probe on X_food
  // Probe on Y_food
  Pull_Resistor pull_resistor_1 (.node(new_apple));
  _4_to_1 u_4_to_1_1 (.in_1(new_apple_t), .out_2(new_apple));
  _4_to_2 u_4_to_2_1 (.in_1(screen_sel), .out_2(n4_to_2_1_out_2));
  Multiplexer #(.select(2)) multiplexer_1 (
    .in0(1'b1), .in1(1'b0), .in2(1'b1), .out(Value), .sel(n4_to_2_1_out_2));  // open: in3, en
  _8_to_1 u_8_to_1_1 (.in_1(is_eaten_t), .out_2(is_eaten));
  assign dir = {{6{1'b0}}, Direction};  // Bit_Extender bit_extender_1
  assign {x_head_t[7:4], head_coords[1:0], x_head_t[1:0]} = {{4{1'b0}}, X_head};  // Bit_Extender bit_extender_2
  assign {y_head_t, head_coords[7:4]} = {{4{1'b0}}, Y_head};  // Bit_Extender bit_extender_3
  assign {x_tail_t[7:4], tail_coords[1:0], x_tail_t[1:0]} = {{4{1'b0}}, X_tail};  // Bit_Extender bit_extender_4
  assign {y_tail_t, tail_coords[7:4]} = {{4{1'b0}}, Y_tail};  // Bit_Extender bit_extender_5
  assign x_food_t = {{4{1'b0}}, X_food};  // Bit_Extender bit_extender_6
  assign y_food_t = {{4{1'b0}}, Y_food};  // Bit_Extender bit_extender_7
  Pull_Resistor pull_resistor_2 (.node(is_eaten));
  _8_to_4 u_8_to_4_1 (.in_1(x_food_t), .out_2(n8_to_4_1_out_2));
  _8_to_4 u_8_to_4_2 (.in_1(y_food_t), .out_2(n8_to_4_2_out_2));
  Multiplexer #(.select(2), .width(4)) multiplexer_2 (
    .in0(out_x_head), .in1(out_x_tail), .in2(n8_to_4_1_out_2), .out(X), .sel(n4_to_2_2_out_2));  // open: in3, en
  _4_to_2 u_4_to_2_2 (.in_1(screen_sel), .out_2(n4_to_2_2_out_2));
  Multiplexer #(.select(2), .width(4)) multiplexer_3 (
    .in0(out_y_head), .in1(out_y_tail), .in2(n8_to_4_2_out_2), .out(Y), .sel(n4_to_2_2_out_2));  // open: in3, en
  Multiplexer #(.select(4), .width(8)) multiplexer_4 (
    .in6({head_coords[7:4], 2'b00, head_coords[1:0]}), .in7({tail_coords[7:4], 2'b00, tail_coords[1:0]}),
    .in8({x_head_t[7:4], head_coords[1:0], x_head_t[1:0]}),
    .in9({x_tail_t[7:4], tail_coords[1:0], x_tail_t[1:0]}), .in10(head_sdvig_5), .in11(tail_sdvig_5),
    .in12(head_dir_sdv), .in13({{6{1'b0}}, tail_dir_sdv}), .in14(dir), .in15(is_eaten_t),
    .out(multiplexer_4_out), .sel(IO_adr));  // open: in0, in1, in2, in3, in4, in5, en
  Register register_1 (.D(multiplexer_4_out), .Q(register_1_q), .clk(not_1_out));  // open: en, clr
  not not_1 (not_1_out, not_2_out);
  not not_2 (not_2_out, and_1_out);
  and and_1 (and_1_out, IO_sel, in_out_prime);
  Pull_Resistor pull_resistor_3 (.node(stop_work_if_1));
  _8_to_4 u_8_to_4_3 (.in_1({x_head_t[7:4], head_coords[1:0], x_head_t[1:0]}), .out_2(n8_to_4_3_out_2));
  _8_to_4 u_8_to_4_4 (.in_1({y_head_t, head_coords[7:4]}), .out_2(n8_to_4_4_out_2));
  _8_to_4 u_8_to_4_5 (.in_1(x_food_t), .out_2(n8_to_4_5_out_2));
  _8_to_4 u_8_to_4_6 (.in_1(y_food_t), .out_2(n8_to_4_6_out_2));
  module_cdm8 module_cdm8_1 (
    .In_out_prime(in_out_prime), .IO_adr(IO_adr), .IO_sel(IO_sel), .IO_output(module_cdm8_1_io_output),
    .IO_input(register_1_q), .stop(stop_work_if_1));  // open: reset
  Pull_Resistor pull_resistor_4 (.node(IO_adr));
  _4_to_2 u_4_to_2_3 (.in_1(head_dir), .out_2(n4_to_2_3_out_2));
  _8_to_4 u_8_to_4_7 (.in_1({x_head_t[7:4], head_coords[1:0], x_head_t[1:0]}), .out_2(n8_to_4_7_out_2));
  _8_to_4 u_8_to_4_8 (.in_1({y_head_t, head_coords[7:4]}), .out_2(n8_to_4_8_out_2));
  _4_to_2 u_4_to_2_4 (.in_1(tail_dir), .out_2(n4_to_2_4_out_2));
  _8_to_4 u_8_to_4_9 (.in_1({x_tail_t[7:4], tail_coords[1:0], x_tail_t[1:0]}), .out_2(n8_to_4_9_out_2));
  _8_to_4 u_8_to_4_10 (.in_1({y_tail_t, tail_coords[7:4]}), .out_2(n8_to_4_10_out_2));
  not not_3 (not_3_out, not_3_out);
  Demultiplexer #(.select(4), .width(8)) demultiplexer_1 (
    .out9(demultiplexer_1_out9), .out10(demultiplexer_1_out10), .out11(demultiplexer_1_out11),
    .out12(demultiplexer_1_out12), .out13(demultiplexer_1_out13), .out14(demultiplexer_1_out14),
    .out15(demultiplexer_1_out15), .in(module_cdm8_1_io_output), .sel(IO_adr), .en(not_4_out));  // open: out0, out1, out2, out3, out4, out5, out6, out7, out8
  not not_4 (not_4_out, in_out_prime);
  not not_5 (not_5_out, move_head);
  not not_6 (not_6_out, move_tail);
  eat_apple eat_apple_1 (
    .head_x(n8_to_4_3_out_2), .head_y(n8_to_4_4_out_2), .apple_x(n8_to_4_5_out_2), .apple_y(n8_to_4_6_out_2),
    .is_eat_apple(eat_apple_1_is_eat_apple));
  _8__3 u_8_3_1 (.in_1(demultiplexer_1_out9), .out_2(n8_3_1_out_2));
  _8_to_4 u_8_to_4_11 (.in_1(demultiplexer_1_out10), .out_2(n8_to_4_11_out_2));
  _8_to_4 u_8_to_4_12 (.in_1(demultiplexer_1_out11), .out_2(n8_to_4_12_out_2));
  _8_to_4 u_8_to_4_13 (.in_1(demultiplexer_1_out12), .out_2(n8_to_4_13_out_2));
  _8_to_4 u_8_to_4_14 (.in_1(demultiplexer_1_out13), .out_2(n8_to_4_14_out_2));
  _8_to_1 u_8_to_1_2 (.in_1(demultiplexer_1_out15), .out_2(n8_to_1_2_out_2));
  change_coords change_coords_1 (
    .update(not_5_out), .Direction(n4_to_2_3_out_2), .X(n8_to_4_7_out_2), .Y(n8_to_4_8_out_2),
    .new_x(out_x_head), .new_y(out_y_head));
  change_coords change_coords_2 (
    .update(not_6_out), .Direction(n4_to_2_4_out_2), .X(n8_to_4_9_out_2), .Y(n8_to_4_10_out_2),
    .new_x(out_x_tail), .new_y(out_y_tail));
  assign is_eaten_t = {{7{1'b0}}, eat_apple_1_is_eat_apple};  // Bit_Extender bit_extender_8
  _4_to_2 u_4_to_2_5 (.in_1(scanned_dir), .out_2(out_15));
  Pull_Resistor pull_resistor_5 (.node(n8_to_1_2_out_2));
  Register #(.width(3)) register_2 (.D(n8_3_1_out_2), .Q(num_of_screen), .clk(and_2_out));  // open: en, clr
  Register #(.width(4)) register_3 (.D(n8_to_4_11_out_2), .Q(head_dir), .clk(move_head));  // open: en, clr
  Register #(.width(4)) register_4 (.D(n8_to_4_12_out_2), .Q(tail_dir), .clk(move_tail));  // open: en, clr
  Register #(.width(4)) register_5 (.D(n8_to_4_13_out_2), .Q(new_apple_t), .clk(and_5_out));  // open: en, clr
  Register #(.width(4)) register_6 (.D(n8_to_4_14_out_2), .Q(screen_sel), .clk(and_6_out));  // open: en, clr
  Register register_7 (.D(demultiplexer_1_out14), .Q(data_line), .clk(and_7_out));  // open: en, clr
  Register #(.width(1)) register_8 (.D(n8_to_1_2_out_2), .Q(check_crash_if_1), .clk(and_8_out));  // open: en, clr
  and and_2 (and_2_out, IO_adr[0], ~IO_adr[1], ~IO_adr[2], IO_adr[3], IO_sel, ~in_out_prime);  // AND_Gate
  and and_3 (move_head, ~IO_adr[0], IO_adr[1], ~IO_adr[2], IO_adr[3], IO_sel, ~in_out_prime);  // AND_Gate
  and and_4 (move_tail, IO_adr[0], IO_adr[1], ~IO_adr[2], IO_adr[3], IO_sel, ~in_out_prime);  // AND_Gate
  and and_5 (and_5_out, ~IO_adr[0], ~IO_adr[1], IO_adr[2], IO_adr[3], IO_sel, ~in_out_prime);  // AND_Gate
  and and_6 (and_6_out, IO_adr[0], ~IO_adr[1], IO_adr[2], IO_adr[3], IO_sel, ~in_out_prime);  // AND_Gate
  and and_7 (and_7_out, ~IO_adr[0], IO_adr[1], IO_adr[2], IO_adr[3], IO_sel, ~in_out_prime);  // AND_Gate
  and and_8 (and_8_out, IO_adr[0], IO_adr[1], IO_adr[2], IO_adr[3], IO_sel, ~in_out_prime);  // AND_Gate
  _8_to_4 u_8_to_4_15 (.in_1(dir), .out_2(n8_to_4_15_out_2));
  Register #(.width(4)) register_9 (.D(n8_to_4_15_out_2), .Q(scanned_dir), .clk(and_9_out));  // open: en, clr
  and and_9 (and_9_out, ~IO_adr[0], IO_adr[1], IO_adr[2], IO_adr[3], IO_sel, in_out_prime);  // AND_Gate
  and and_10 (and_10_out, ~IO_adr[0], IO_adr[1], IO_adr[2], IO_adr[3], IO_sel, in_out_prime);  // AND_Gate
  assign and_11_out = {x_head_t[7:4], head_coords[1:0], x_head_t[1:0]} & 8'h3;  // AND_Gate and_11, 8 bits wide
  assign and_12_out = {x_tail_t[7:4], tail_coords[1:0], x_tail_t[1:0]} & 8'h3;  // AND_Gate and_12, 8 bits wide
  Register register_10 (.D(dir), .Q(register_10_q), .clk(and_10_out));  // open: en, clr
  Shifter #(.shift("lr")) shifter_1 (.in(8'hc0), .\dist ({and_11_out[1:0], 1'b0}), .out(head_sdvig_5));
  Shifter #(.shift("lr")) shifter_2 (.in(8'hc0), .\dist ({and_12_out[1:0], 1'b0}), .out(tail_sdvig_5));
  Shifter #(.shift("lr")) shifter_3 (
    .in({register_10_q[1:0], {6{1'b0}}}), .\dist ({and_11_out[1:0], 1'b0}), .out(head_dir_sdv));
  Shifter shifter_4 (.in(data_line), .\dist ({and_12_out[1:0], 1'b0}), .out({tail_dir_sdv, shifter_4_out}));

  // Other names for the same wires on the sheet: check_crash = check_crash_if_1; x_head_t[3:2] = head_coords[1:0];
  //   y_head_t[3:0] = head_coords[7:4]; stop_if_1 = stop_work_if_1; x_tail_t[3:2] = tail_coords[1:0];
  //   y_tail_t[3:0] = tail_coords[7:4]; x_head_new[3:0] = out_x_head; x_tail_new[3:0] = out_x_tail;
  //   y_head_new[3:0] = out_y_head; y_tail_new[3:0] = out_y_tail

  // Notes on the sheet:
  //   X: pull=down
  //   Y: pull=down
  //   INPUT
  //   Create Adress in memory
  //   Cdm-8 IO/In
  //   OUTPUT
  //   Work with Cdm-8
  //   Change coords
  //   Сhecking whether the apple is eaten
  //   Cdm-8 IO/Out
  //   Help cdm-8 take/save direction to RAM
endmodule

module data_to_screen (
  input  clock,
  input  [3:0] X,
  input  [3:0] Y,
  input  Value,
  input  Stop,
  input  request,
  input  [3:0] Y_FOOD,
  input  [3:0] Y_Head,
  input  [3:0] X_FOOD,
  input  [3:0] X_Head,
  output [15:0] out_11,
  output [15:0] out_12,
  output [15:0] out_13,
  output [15:0] out_14,
  output [15:0] out_15,
  output [15:0] out_16,
  output [15:0] out_17,
  output [15:0] out_18,
  output [15:0] out_19,
  output [15:0] out_20,
  output [15:0] out_21,
  output [15:0] out_22,
  output [15:0] out_23,
  output [15:0] out_24,
  output [15:0] out_25,
  output [15:0] out_26,
  output Err,
  output crash
);

  wire _0_out, _1_out, _2_out, _3_out, _4_out, _5_out, _6_out, _7_out, _8_out, _9_out, _10_a_out, _11_b_out,
       _12_c_out, _13_d_out, _14_e_out, _15_f_out, and_17_out, comparator_1_eq, comparator_2_eq,
       multiplexer_2_out, multiplexer_36_out, not_1_out, not_2_out, not_3_out, not_4_out, not_5_out,
       not_6_out, not_7_out, not_8_out, not_9_out, not_10_out, not_11_out, not_12_out, not_13_out,
       not_14_out, not_15_out, not_16_out, or_17_out, or_18_out, or_19_out, or_20_out, or_21_out, or_22_out,
       or_23_out, or_24_out, or_25_out, or_26_out, or_27_out, or_28_out, or_29_out, or_30_out, or_31_out,
       or_32_out;
  wire [3:0] subtractor_1_out, subtractor_2_out;
  wire [15:0] and_1_out, and_2_out, and_3_out, and_4_out, and_5_out, and_6_out, and_7_out, and_8_out,
       and_9_out, and_10_out, and_11_out, and_12_out, and_13_out, and_14_out, and_15_out, and_16_out,
       multiplexer_1_out, multiplexer_3_out, multiplexer_4_out, multiplexer_5_out, multiplexer_6_out,
       multiplexer_7_out, multiplexer_8_out, multiplexer_9_out, multiplexer_10_out, multiplexer_11_out,
       multiplexer_12_out, multiplexer_13_out, multiplexer_14_out, multiplexer_15_out, multiplexer_16_out,
       multiplexer_17_out, multiplexer_18_out, multiplexer_19_out, multiplexer_20_out, multiplexer_21_out,
       multiplexer_22_out, multiplexer_23_out, multiplexer_24_out, multiplexer_25_out, multiplexer_26_out,
       multiplexer_27_out, multiplexer_28_out, multiplexer_29_out, multiplexer_30_out, multiplexer_31_out,
       multiplexer_32_out, multiplexer_33_out, multiplexer_34_out, multiplexer_35_out, or_1_out, or_2_out,
       or_3_out, or_4_out, or_5_out, or_6_out, or_7_out, or_8_out, or_9_out, or_10_out, or_11_out, or_12_out,
       or_13_out, or_14_out, or_15_out, or_16_out, shifter_1_out, shifter_2_out, shifter_3_out,
       shifter_4_out, shifter_5_out, shifter_6_out, shifter_7_out, shifter_8_out, shifter_9_out,
       shifter_10_out, shifter_11_out, shifter_12_out, shifter_13_out, shifter_14_out, shifter_15_out,
       shifter_16_out;

  Pull_Resistor pull_resistor_1 (.node(Value));
  Pull_Resistor pull_resistor_2 (.node(Stop));
  Multiplexer #(.select(4), .width(16)) multiplexer_1 (
    .in0(out_11), .in1(out_12), .in2(out_13), .in3(out_14), .in4(out_15), .in5(out_16), .in6(out_17),
    .in7(out_18), .in8(out_19), .in9(out_20), .in10(out_21), .in11(out_22), .in12(out_23), .in13(out_24),
    .in14(out_25), .in15(out_26), .out(multiplexer_1_out), .sel(Y_FOOD));  // open: en
  Multiplexer #(.select(4)) multiplexer_2 (
    .in0(multiplexer_1_out[0]), .in1(multiplexer_1_out[1]), .in2(multiplexer_1_out[2]),
    .in3(multiplexer_1_out[3]), .in4(multiplexer_1_out[4]), .in5(multiplexer_1_out[5]),
    .in6(multiplexer_1_out[6]), .in7(multiplexer_1_out[7]), .in8(multiplexer_1_out[8]),
    .in9(multiplexer_1_out[9]), .in10(multiplexer_1_out[10]), .in11(multiplexer_1_out[11]),
    .in12(multiplexer_1_out[12]), .in13(multiplexer_1_out[13]), .in14(multiplexer_1_out[14]),
    .in15(multiplexer_1_out[15]), .out(multiplexer_2_out), .sel(subtractor_1_out));  // open: en
  Shifter #(.width(16), .shift("lr")) shifter_1 (.in(16'h8000), .\dist (X), .out(shifter_1_out));
  Shifter #(.width(16), .shift("lr")) shifter_2 (.in(16'h8000), .\dist (X), .out(shifter_2_out));
  Shifter #(.width(16), .shift("lr")) shifter_3 (.in(16'h8000), .\dist (X), .out(shifter_3_out));
  Shifter #(.width(16), .shift("lr")) shifter_4 (.in(16'h8000), .\dist (X), .out(shifter_4_out));
  Shifter #(.width(16), .shift("lr")) shifter_5 (.in(16'h8000), .\dist (X), .out(shifter_5_out));
  Shifter #(.width(16), .shift("lr")) shifter_6 (.in(16'h8000), .\dist (X), .out(shifter_6_out));
  Shifter #(.width(16), .shift("lr")) shifter_7 (.in(16'h8000), .\dist (X), .out(shifter_7_out));
  Shifter #(.width(16), .shift("lr")) shifter_8 (.in(16'h8000), .\dist (X), .out(shifter_8_out));
  Shifter #(.width(16), .shift("lr")) shifter_9 (.in(16'h8000), .\dist (X), .out(shifter_9_out));
  Shifter #(.width(16), .shift("lr")) shifter_10 (.in(16'h8000), .\dist (X), .out(shifter_10_out));
  Shifter #(.width(16), .shift("lr")) shifter_11 (.in(16'h8000), .\dist (X), .out(shifter_11_out));
  Shifter #(.width(16), .shift("lr")) shifter_12 (.in(16'h8000), .\dist (X), .out(shifter_12_out));
  Shifter #(.width(16), .shift("lr")) shifter_13 (.in(16'h8000), .\dist (X), .out(shifter_13_out));
  Shifter #(.width(16), .shift("lr")) shifter_14 (.in(16'h8000), .\dist (X), .out(shifter_14_out));
  Shifter #(.width(16), .shift("lr")) shifter_15 (.in(16'h8000), .\dist (X), .out(shifter_15_out));
  Shifter #(.width(16), .shift("lr")) shifter_16 (.in(16'h8000), .\dist (X), .out(shifter_16_out));
  Comparator #(.width(4)) comparator_1 (.a(X_Head), .b(X_FOOD), .eq(comparator_1_eq));  // open: gt, lt
  Comparator #(.width(4)) comparator_2 (.a(Y_Head), .b(Y_FOOD), .eq(comparator_2_eq));  // open: gt, lt
  // Probe on subtractor_1_out
  Subtractor #(.width(4)) subtractor_1 (.a(4'b1111), .b(X_FOOD), .out(subtractor_1_out));  // open: bin, bout
  assign and_1_out = ~shifter_1_out & out_11;  // AND_Gate and_1, 16 bits wide
  Multiplexer #(.width(16)) multiplexer_3 (
    .in0(and_1_out), .in1(or_1_out), .out(multiplexer_3_out), .sel(Value));  // open: en
  assign or_1_out = out_11 | shifter_1_out;  // OR_Gate or_1, 16 bits wide
  not not_1 (not_1_out, _0_out);
  and _0 (_0_out, ~Y[0], ~Y[1], ~Y[2], ~Y[3]);  // AND_Gate
  assign and_2_out = ~shifter_2_out & out_12;  // AND_Gate and_2, 16 bits wide
  Multiplexer #(.width(16)) multiplexer_4 (
    .in0(and_2_out), .in1(or_2_out), .out(multiplexer_4_out), .sel(Value));  // open: en
  assign or_2_out = out_12 | shifter_2_out;  // OR_Gate or_2, 16 bits wide
  and _1 (_1_out, Y[0], ~Y[1], ~Y[2], ~Y[3]);  // AND_Gate
  not not_2 (not_2_out, _1_out);
  assign and_3_out = ~shifter_3_out & out_13;  // AND_Gate and_3, 16 bits wide
  Multiplexer #(.width(16)) multiplexer_5 (
    .in0(and_3_out), .in1(or_3_out), .out(multiplexer_5_out), .sel(Value));  // open: en
  assign or_3_out = out_13 | shifter_3_out;  // OR_Gate or_3, 16 bits wide
  and _2 (_2_out, ~Y[0], Y[1], ~Y[2], ~Y[3]);  // AND_Gate
  not not_3 (not_3_out, _2_out);
  assign and_4_out = ~shifter_4_out & out_14;  // AND_Gate and_4, 16 bits wide
  Multiplexer #(.width(16)) multiplexer_6 (
    .in0(and_4_out), .in1(or_4_out), .out(multiplexer_6_out), .sel(Value));  // open: en
  assign or_4_out = out_14 | shifter_4_out;  // OR_Gate or_4, 16 bits wide
  and _3 (_3_out, Y[0], Y[1], ~Y[2], ~Y[3]);  // AND_Gate
  not not_4 (not_4_out, _3_out);
  assign and_5_out = ~shifter_5_out & out_15;  // AND_Gate and_5, 16 bits wide
  Multiplexer #(.width(16)) multiplexer_7 (
    .in0(and_5_out), .in1(or_5_out), .out(multiplexer_7_out), .sel(Value));  // open: en
  assign or_5_out = out_15 | shifter_5_out;  // OR_Gate or_5, 16 bits wide
  and _4 (_4_out, ~Y[0], ~Y[1], Y[2], ~Y[3]);  // AND_Gate
  not not_5 (not_5_out, _4_out);
  assign and_6_out = ~shifter_6_out & out_16;  // AND_Gate and_6, 16 bits wide
  Multiplexer #(.width(16)) multiplexer_8 (
    .in0(and_6_out), .in1(or_6_out), .out(multiplexer_8_out), .sel(Value));  // open: en
  assign or_6_out = out_16 | shifter_6_out;  // OR_Gate or_6, 16 bits wide
  not not_6 (not_6_out, _5_out);
  and _5 (_5_out, Y[0], ~Y[1], Y[2], ~Y[3]);  // AND_Gate
  assign and_7_out = ~shifter_7_out & out_17;  // AND_Gate and_7, 16 bits wide
  Multiplexer #(.width(16)) multiplexer_9 (
    .in0(and_7_out), .in1(or_7_out), .out(multiplexer_9_out), .sel(Value));  // open: en
  assign or_7_out = out_17 | shifter_7_out;  // OR_Gate or_7, 16 bits wide
  not not_7 (not_7_out, _6_out);
  and _6 (_6_out, ~Y[0], Y[1], Y[2], ~Y[3]);  // AND_Gate
  assign and_8_out = ~shifter_8_out & out_18;  // AND_Gate and_8, 16 bits wide
  Multiplexer #(.width(16)) multiplexer_10 (
    .in0(and_8_out), .in1(or_8_out), .out(multiplexer_10_out), .sel(Value));  // open: en
  assign or_8_out = out_18 | shifter_8_out;  // OR_Gate or_8, 16 bits wide
  not not_8 (not_8_out, _7_out);
  and _7 (_7_out, Y[0], Y[1], Y[2], ~Y[3]);  // AND_Gate
  assign and_9_out = ~shifter_9_out & out_19;  // AND_Gate and_9, 16 bits wide
  Multiplexer #(.width(16)) multiplexer_11 (
    .in0(and_9_out), .in1(or_9_out), .out(multiplexer_11_out), .sel(Value));  // open: en
  assign or_9_out = out_19 | shifter_9_out;  // OR_Gate or_9, 16 bits wide
  and _8 (_8_out, ~Y[0], ~Y[1], ~Y[2], Y[3]);  // AND_Gate
  not not_9 (not_9_out, _8_out);
  assign and_10_out = ~shifter_10_out & out_20;  // AND_Gate and_10, 16 bits wide
  Multiplexer #(.width(16)) multiplexer_12 (
    .in0(and_10_out), .in1(or_10_out), .out(multiplexer_12_out), .sel(Value));  // open: en
  assign or_10_out = out_20 | shifter_10_out;  // OR_Gate or_10, 16 bits wide
  not not_10 (not_10_out, _9_out);
  and _9 (_9_out, Y[0], ~Y[1], ~Y[2], Y[3]);  // AND_Gate
  assign and_11_out = ~shifter_11_out & out_21;  // AND_Gate and_11, 16 bits wide
  Multiplexer #(.width(16)) multiplexer_13 (
    .in0(and_11_out), .in1(or_11_out), .out(multiplexer_13_out), .sel(Value));  // open: en
  assign or_11_out = out_21 | shifter_11_out;  // OR_Gate or_11, 16 bits wide
  not not_11 (not_11_out, _10_a_out);
  and _10_a (_10_a_out, ~Y[0], Y[1], ~Y[2], Y[3]);  // AND_Gate
  assign and_12_out = ~shifter_12_out & out_22;  // AND_Gate and_12, 16 bits wide
  Multiplexer #(.width(16)) multiplexer_14 (
    .in0(and_12_out), .in1(or_12_out), .out(multiplexer_14_out), .sel(Value));  // open: en
  assign or_12_out = out_22 | shifter_12_out;  // OR_Gate or_12, 16 bits wide
  not not_12 (not_12_out, _11_b_out);
  and _11_b (_11_b_out, Y[0], Y[1], ~Y[2], Y[3]);  // AND_Gate
  assign and_13_out = ~shifter_13_out & out_23;  // AND_Gate and_13, 16 bits wide
  Multiplexer #(.width(16)) multiplexer_15 (
    .in0(and_13_out), .in1(or_13_out), .out(multiplexer_15_out), .sel(Value));  // open: en
  assign or_13_out = out_23 | shifter_13_out;  // OR_Gate or_13, 16 bits wide
  not not_13 (not_13_out, _12_c_out);
  and _12_c (_12_c_out, ~Y[0], ~Y[1], Y[2], Y[3]);  // AND_Gate
  assign and_14_out = ~shifter_14_out & out_24;  // AND_Gate and_14, 16 bits wide
  Multiplexer #(.width(16)) multiplexer_16 (
    .in0(and_14_out), .in1(or_14_out), .out(multiplexer_16_out), .sel(Value));  // open: en
  assign or_14_out = out_24 | shifter_14_out;  // OR_Gate or_14, 16 bits wide
  and _13_d (_13_d_out, Y[0], ~Y[1], Y[2], Y[3]);  // AND_Gate
  not not_14 (not_14_out, _13_d_out);
  assign and_15_out = ~shifter_15_out & out_25;  // AND_Gate and_15, 16 bits wide
  Multiplexer #(.width(16)) multiplexer_17 (
    .in0(and_15_out), .in1(or_15_out), .out(multiplexer_17_out), .sel(Value));  // open: en
  assign or_15_out = out_25 | shifter_15_out;  // OR_Gate or_15, 16 bits wide
  not not_15 (not_15_out, _14_e_out);
  and _14_e (_14_e_out, ~Y[0], Y[1], Y[2], Y[3]);  // AND_Gate
  assign and_16_out = ~shifter_16_out & out_26;  // AND_Gate and_16, 16 bits wide
  Multiplexer #(.width(16)) multiplexer_18 (
    .in0(and_16_out), .in1(or_16_out), .out(multiplexer_18_out), .sel(Value));  // open: en
  assign or_16_out = out_26 | shifter_16_out;  // OR_Gate or_16, 16 bits wide
  and _15_f (_15_f_out, Y[0], Y[1], Y[2], Y[3]);
  not not_16 (not_16_out, _15_f_out);
  and and_17 (and_17_out, comparator_1_eq, comparator_2_eq);
  or or_17 (or_17_out, Stop, not_1_out);
  or or_18 (or_18_out, Stop, not_2_out);
  or or_19 (or_19_out, Stop, not_3_out);
  or or_20 (or_20_out, Stop, not_4_out);
  or or_21 (or_21_out, Stop, not_5_out);
  or or_22 (or_22_out, Stop, not_6_out);
  or or_23 (or_23_out, Stop, not_7_out);
  or or_24 (or_24_out, Stop, not_8_out);
  or or_25 (or_25_out, Stop, not_9_out);
  or or_26 (or_26_out, Stop, not_10_out);
  or or_27 (or_27_out, Stop, not_11_out);
  or or_28 (or_28_out, Stop, not_12_out);
  or or_29 (or_29_out, Stop, not_13_out);
  or or_30 (or_30_out, Stop, not_14_out);
  or or_31 (or_31_out, Stop, not_15_out);
  or or_32 (or_32_out, Stop, not_16_out);
  or or_33 (Err, and_17_out, multiplexer_2_out);
  Multiplexer #(.width(16)) multiplexer_19 (
    .in0(multiplexer_3_out), .in1(out_11), .out(multiplexer_19_out), .sel(or_17_out));  // open: en
  Register #(.width(16)) register_1 (.D(multiplexer_19_out), .Q(out_11), .clk(clock));  // open: en, clr
  Register #(.width(16)) register_2 (.D(multiplexer_20_out), .Q(out_12), .clk(clock));  // open: en, clr
  Multiplexer #(.width(16)) multiplexer_20 (
    .in0(multiplexer_4_out), .in1(out_12), .out(multiplexer_20_out), .sel(or_18_out));  // open: en
  Register #(.width(16)) register_3 (.D(multiplexer_21_out), .Q(out_13), .clk(clock));  // open: en, clr
  Multiplexer #(.width(16)) multiplexer_21 (
    .in0(multiplexer_5_out), .in1(out_13), .out(multiplexer_21_out), .sel(or_19_out));  // open: en
  Multiplexer #(.width(16)) multiplexer_22 (
    .in0(multiplexer_6_out), .in1(out_14), .out(multiplexer_22_out), .sel(or_20_out));  // open: en
  Register #(.width(16)) register_4 (.D(multiplexer_22_out), .Q(out_14), .clk(clock));  // open: en, clr
  Register #(.width(16)) register_5 (.D(multiplexer_23_out), .Q(out_15), .clk(clock));  // open: en, clr
  Multiplexer #(.width(16)) multiplexer_23 (
    .in0(multiplexer_7_out), .in1(out_15), .out(multiplexer_23_out), .sel(or_21_out));  // open: en
  Multiplexer #(.width(16)) multiplexer_24 (
    .in0(multiplexer_8_out), .in1(out_16), .out(multiplexer_24_out), .sel(or_22_out));  // open: en
  Register #(.width(16)) register_6 (.D(multiplexer_24_out), .Q(out_16), .clk(clock));  // open: en, clr
  Multiplexer #(.width(16)) multiplexer_25 (
    .in0(multiplexer_9_out), .in1(out_17), .out(multiplexer_25_out), .sel(or_23_out));  // open: en
  Register #(.width(16)) register_7 (.D(multiplexer_25_out), .Q(out_17), .clk(clock));  // open: en, clr
  Multiplexer #(.width(16)) multiplexer_26 (
    .in0(multiplexer_10_out), .in1(out_18), .out(multiplexer_26_out), .sel(or_24_out));  // open: en
  Register #(.width(16)) register_8 (.D(multiplexer_26_out), .Q(out_18), .clk(clock));  // open: en, clr
  Multiplexer #(.width(16)) multiplexer_27 (
    .in0(multiplexer_11_out), .in1(out_19), .out(multiplexer_27_out), .sel(or_25_out));  // open: en
  Register #(.width(16)) register_9 (.D(multiplexer_27_out), .Q(out_19), .clk(clock));  // open: en, clr
  Register #(.width(16)) register_10 (.D(multiplexer_28_out), .Q(out_20), .clk(clock));  // open: en, clr
  Multiplexer #(.width(16)) multiplexer_28 (
    .in0(multiplexer_12_out), .in1(out_20), .out(multiplexer_28_out), .sel(or_26_out));  // open: en
  Multiplexer #(.width(16)) multiplexer_29 (
    .in0(multiplexer_13_out), .in1(out_21), .out(multiplexer_29_out), .sel(or_27_out));  // open: en
  Register #(.width(16)) register_11 (.D(multiplexer_29_out), .Q(out_21), .clk(clock));  // open: en, clr
  Multiplexer #(.width(16)) multiplexer_30 (
    .in0(multiplexer_14_out), .in1(out_22), .out(multiplexer_30_out), .sel(or_28_out));  // open: en
  Register #(.width(16)) register_12 (.D(multiplexer_30_out), .Q(out_22), .clk(clock));  // open: en, clr
  Multiplexer #(.width(16)) multiplexer_31 (
    .in0(multiplexer_15_out), .in1(out_23), .out(multiplexer_31_out), .sel(or_29_out));  // open: en
  Register #(.width(16)) register_13 (.D(multiplexer_31_out), .Q(out_23), .clk(clock));  // open: en, clr
  Multiplexer #(.width(16)) multiplexer_32 (
    .in0(multiplexer_16_out), .in1(out_24), .out(multiplexer_32_out), .sel(or_30_out));  // open: en
  Register #(.width(16)) register_14 (.D(multiplexer_32_out), .Q(out_24), .clk(clock));  // open: en, clr
  Register #(.width(16)) register_15 (.D(multiplexer_33_out), .Q(out_25), .clk(clock));  // open: en, clr
  Multiplexer #(.width(16)) multiplexer_33 (
    .in0(multiplexer_17_out), .in1(out_25), .out(multiplexer_33_out), .sel(or_31_out));  // open: en
  Multiplexer #(.width(16)) multiplexer_34 (
    .in0(multiplexer_18_out), .in1(out_26), .out(multiplexer_34_out), .sel(or_32_out));  // open: en
  Register #(.width(16)) register_16 (.D(multiplexer_34_out), .Q(out_26), .clk(clock));  // open: en, clr
  Multiplexer #(.select(4), .width(16)) multiplexer_35 (
    .in0(out_11), .in1(out_12), .in2(out_13), .in3(out_14), .in4(out_15), .in5(out_16), .in6(out_17),
    .in7(out_18), .in8(out_19), .in9(out_20), .in10(out_21), .in11(out_22), .in12(out_23), .in13(out_24),
    .in14(out_25), .in15(out_26), .out(multiplexer_35_out), .sel(Y_Head));  // open: en
  Multiplexer #(.select(4)) multiplexer_36 (
    .in0(multiplexer_35_out[0]), .in1(multiplexer_35_out[1]), .in2(multiplexer_35_out[2]),
    .in3(multiplexer_35_out[3]), .in4(multiplexer_35_out[4]), .in5(multiplexer_35_out[5]),
    .in6(multiplexer_35_out[6]), .in7(multiplexer_35_out[7]), .in8(multiplexer_35_out[8]),
    .in9(multiplexer_35_out[9]), .in10(multiplexer_35_out[10]), .in11(multiplexer_35_out[11]),
    .in12(multiplexer_35_out[12]), .in13(multiplexer_35_out[13]), .in14(multiplexer_35_out[14]),
    .in15(multiplexer_35_out[15]), .out(multiplexer_36_out), .sel(subtractor_2_out));  // open: en
  // Probe on subtractor_2_out
  Subtractor #(.width(4)) subtractor_2 (.a(4'b1111), .b(X_Head), .out(subtractor_2_out));  // open: bin, bout
  and and_18 (crash, multiplexer_36_out, request);
  Pull_Resistor pull_resistor_3 (.node(crash));

  // Other names for the same wires on the sheet: _0[15:0] = out_11; _1[15:0] = out_12; _2[15:0] = out_13;
  //   _3[15:0] = out_14; _4[15:0] = out_15; _5[15:0] = out_16; _6[15:0] = out_17; _7[15:0] = out_18;
  //   _8[15:0] = out_19; _9[15:0] = out_20; _10[15:0] = out_21; _11[15:0] = out_22; _12[15:0] = out_23;
  //   _13[15:0] = out_24; _14[15:0] = out_25; _15[15:0] = out_26; food_x[3:0] = X_FOOD; food_y[3:0] = Y_FOOD;
  //   head_x[3:0] = X_Head; head_y[3:0] = Y_Head

  // Notes on the sheet:
  //   Circiut to save and change the field
  //   Check to avoid generating apples on the snake's body
  //   Main field 
  //   Checking for a collision of the snake's head with the body
endmodule

module direction (
  input  [1:0] cur_dir,
  input  UP,
  input  DOWN,
  input  Clock,
  input  LEFT,
  input  RIGHT,
  output [1:0] State
);

  wire _0_out, _1_out, _2_out, _3_out, and_1_out, and_2_out, and_3_out, and_4_out, or_1_out, or_2_out,
       or_3_out, or_4_out;
  wire [1:0] transistor_1_out;

  and _1 (_1_out, cur_dir[0], ~cur_dir[1]);  // AND_Gate
  and _0 (_0_out, ~cur_dir[0], ~cur_dir[1]);  // AND_Gate
  and _3 (_3_out, cur_dir[0], cur_dir[1]);
  and _2 (_2_out, ~cur_dir[0], cur_dir[1]);  // AND_Gate
  or or_1 (or_1_out, DOWN, LEFT, RIGHT);
  or or_2 (or_2_out, UP, LEFT, RIGHT);
  or or_3 (or_3_out, UP, DOWN, RIGHT);
  or or_4 (or_4_out, UP, DOWN, LEFT);
  and and_1 (and_1_out, ~or_1_out, ~_1_out, UP);  // AND_Gate
  Transistor #(.\type ("n"), .width(2)) transistor_1 (.in(2'b00), .out(transistor_1_out), .gate(and_1_out));
  and and_2 (and_2_out, ~or_2_out, ~_0_out, DOWN);  // AND_Gate
  Transistor #(.\type ("n"), .width(2)) transistor_2 (.in(2'b01), .out(transistor_1_out), .gate(and_2_out));
  and and_3 (and_3_out, ~or_3_out, ~_3_out, LEFT);  // AND_Gate
  Transistor #(.\type ("n"), .width(2)) transistor_3 (.in(2'b10), .out(transistor_1_out), .gate(and_3_out));
  and and_4 (and_4_out, ~or_4_out, ~_2_out, RIGHT);  // AND_Gate
  Transistor #(.\type ("n"), .width(2)) transistor_4 (.in(2'b11), .out(transistor_1_out), .gate(and_4_out));
  Register #(.width(2)) register_1 (.D(transistor_1_out), .Q(State), .clk(Clock));  // open: en, clr

  // Other names for the same wires on the sheet: D = DOWN; L = LEFT; R = RIGHT; U = UP

  // Notes on the sheet:
  //   State: pull=down
  //   Changing the data entered from the keyboard
  //   Checking that snake will not backtrack over its body
endmodule

module coords (
  input  Clock,
  input  [3:0] X,
  input  [3:0] Y,
  output [3:0] out_4,
  output [3:0] out_5
);

  Register #(.width(4)) register_1 (.D(X), .Q(out_4), .clk(Clock));  // open: en, clr
  Register #(.width(4)) register_2 (.D(Y), .Q(out_5), .clk(Clock));  // open: en, clr

  // Notes on the sheet:
  //   Circuit for saving and changing coordinates
endmodule

module update_to_screen (
  input  update,
  input  [15:0] in_2,
  input  [15:0] in_3,
  input  [15:0] in_4,
  input  [15:0] in_5,
  input  [15:0] in_6,
  input  [15:0] in_7,
  input  [15:0] in_8,
  input  [15:0] in_9,
  input  [15:0] in_10,
  input  [15:0] in_11,
  input  [15:0] in_12,
  input  [15:0] in_13,
  input  [15:0] in_14,
  input  [15:0] in_15,
  input  [15:0] in_16,
  input  [15:0] in_17,
  output [15:0] out_18,
  output [15:0] out_19,
  output [15:0] out_20,
  output [15:0] out_21,
  output [15:0] out_22,
  output [15:0] out_23,
  output [15:0] out_24,
  output [15:0] out_25,
  output [15:0] out_26,
  output [15:0] out_27,
  output [15:0] out_28,
  output [15:0] out_29,
  output [15:0] out_30,
  output [15:0] out_31,
  output [15:0] out_32,
  output [15:0] out_33
);

  Register #(.width(16)) register_1 (.D(in_2), .Q(out_18), .clk(update));  // open: en, clr
  Register #(.width(16)) register_2 (.D(in_3), .Q(out_19), .clk(update));  // open: en, clr
  Register #(.width(16)) register_3 (.D(in_4), .Q(out_20), .clk(update));  // open: en, clr
  Register #(.width(16)) register_4 (.D(in_5), .Q(out_21), .clk(update));  // open: en, clr
  Register #(.width(16)) register_5 (.D(in_6), .Q(out_22), .clk(update));  // open: en, clr
  Register #(.width(16)) register_6 (.D(in_7), .Q(out_23), .clk(update));  // open: en, clr
  Register #(.width(16)) register_7 (.D(in_8), .Q(out_24), .clk(update));  // open: en, clr
  Register #(.width(16)) register_8 (.D(in_9), .Q(out_25), .clk(update));  // open: en, clr
  Register #(.width(16)) register_9 (.D(in_10), .Q(out_26), .clk(update));  // open: en, clr
  Register #(.width(16)) register_10 (.D(in_11), .Q(out_27), .clk(update));  // open: en, clr
  Register #(.width(16)) register_11 (.D(in_12), .Q(out_28), .clk(update));  // open: en, clr
  Register #(.width(16)) register_12 (.D(in_13), .Q(out_29), .clk(update));  // open: en, clr
  Register #(.width(16)) register_13 (.D(in_14), .Q(out_30), .clk(update));  // open: en, clr
  Register #(.width(16)) register_14 (.D(in_15), .Q(out_31), .clk(update));  // open: en, clr
  Register #(.width(16)) register_15 (.D(in_16), .Q(out_32), .clk(update));  // open: en, clr
  Register #(.width(16)) register_16 (.D(in_17), .Q(out_33), .clk(update));  // open: en, clr
endmodule

module keyboard_input (
  input  [6:0] in_1,
  output left,
  output up,
  output right,
  output down
);

  wire comparator_1_eq, comparator_2_eq, comparator_3_eq, comparator_4_eq, comparator_5_eq, comparator_6_eq,
       comparator_7_eq, comparator_8_eq;

  Comparator #(.width(7)) comparator_1 (.a(in_1), .b(7'b1100001), .eq(comparator_1_eq));  // open: gt, lt
  Comparator #(.width(7)) comparator_2 (.a(in_1), .b(7'b1000100), .eq(comparator_2_eq));  // open: gt, lt
  Comparator #(.width(7)) comparator_3 (.a(in_1), .b(7'b1100100), .eq(comparator_3_eq));  // open: gt, lt
  Comparator #(.width(7)) comparator_4 (.a(in_1), .b(7'b0110010), .eq(comparator_4_eq));  // open: gt, lt
  or or_1 (right, comparator_3_eq, comparator_4_eq);
  or or_2 (left, comparator_1_eq, comparator_2_eq);
  Comparator #(.width(7)) comparator_5 (.a(in_1), .b(7'b1110111), .eq(comparator_5_eq));  // open: gt, lt
  Comparator #(.width(7)) comparator_6 (.a(in_1), .b(7'b1000110), .eq(comparator_6_eq));  // open: gt, lt
  Comparator #(.width(7)) comparator_7 (.a(in_1), .b(7'b1110011), .eq(comparator_7_eq));  // open: gt, lt
  Comparator #(.width(7)) comparator_8 (.a(in_1), .b(7'b1001011), .eq(comparator_8_eq));  // open: gt, lt
  or or_3 (up, comparator_5_eq, comparator_6_eq);
  or or_4 (down, comparator_7_eq, comparator_8_eq);

  // Other names for the same wires on the sheet: ascii[6:0] = in_1

  // Notes on the sheet:
  //   Left
  //   Right
  //   Entering data from the keyboard and changing it to the direction
  //   Up
  //   Down
endmodule

module module_cdm8 (
  input  stop,
  input  [7:0] IO_input,
  output In_out_prime,
  output [3:0] IO_adr,
  output IO_sel,
  output reset,
  output [7:0] IO_output
);

  wire _4_f_out, and_1_out, and_4_out, cdm_8_1_data_code_prime, cl, code, data, E_out, F_out, mem, not_1_out,
       not_2_out, not_3_out, or_1_out, pull_resistor_1_node, RAM;
  wire [7:0] cdm_8_1_data_out, cdm_8_1_ps, cdm_8_1_r0, cdm_8_1_r1, cdm_8_1_r2, cdm_8_1_r3, cdm_8_1_sp,
       controlled_buffer_3_out;
  wire [7:4] cdm_8_1_addr;

  assign IO_output = and_1_out ? IO_input : 8'bz;  // Controlled_Buffer controlled_buffer_1
  and and_1 (and_1_out, In_out_prime, IO_sel);
  // Probe on cdm_8_1_r0
  // Probe on cdm_8_1_r1
  // Probe on cdm_8_1_r2
  Pull_Resistor pull_resistor_1 (.node(pull_resistor_1_node));
  Transistor transistor_1 (.in(cl), .out(pull_resistor_1_node), .gate(stop));
  Clock clock_1 (.out(cl));
  and and_2 (IO_sel, not_1_out, cl, data);
  // Probe on cdm_8_1_r3
  // Probe on cdm_8_1_sp
  not not_1 (not_1_out, not_2_out);
  // Probe on cdm_8_1_ps
  CdM_8 cdm_8_1 (
    .data_code_prime(cdm_8_1_data_code_prime), .R0(cdm_8_1_r0), .R1(cdm_8_1_r1), .mem(mem), .R2(cdm_8_1_r2),
    .load_st_prime(In_out_prime), .R3(cdm_8_1_r3), .addr({cdm_8_1_addr, IO_adr}), .SP(cdm_8_1_sp),
    .data_out(cdm_8_1_data_out), .data_in(controlled_buffer_3_out), .PS(cdm_8_1_ps),
    .clk(pull_resistor_1_node));  // open: PC, page, rset, IAck, IRQ, vector, shadow
  not not_2 (not_2_out, and_4_out);
  and and_3 (RAM, not_2_out, data);
  assign IO_output = not_3_out ? cdm_8_1_data_out : 8'bz;  // Controlled_Buffer controlled_buffer_2
  not not_3 (not_3_out, In_out_prime);
  assign controlled_buffer_3_out = In_out_prime ? IO_output : 8'bz;  // Controlled_Buffer controlled_buffer_3
  and and_4 (and_4_out, or_1_out, _4_f_out);
  Decoder #(.disabled(0)) decoder_1 (.out0(code), .out1(data), .sel(cdm_8_1_data_code_prime), .en(mem));
  or or_1 (or_1_out, F_out, E_out);
  Pull_Resistor pull_resistor_2 (.node({cdm_8_1_addr, IO_adr}));
  and F (F_out, cdm_8_1_addr[4], cdm_8_1_addr[5], cdm_8_1_addr[6], cdm_8_1_addr[7]);
  and E (E_out, ~cdm_8_1_addr[4], cdm_8_1_addr[5], cdm_8_1_addr[6], cdm_8_1_addr[7]);  // AND_Gate
  or _4_f (_4_f_out, IO_adr[2], IO_adr[3]);
  ROM rom_1 (.addr({cdm_8_1_addr, IO_adr}), .data(IO_output), .sel(code));
  RAM ram_1 (.addr({cdm_8_1_addr, IO_adr}), .data(IO_output), .sel(RAM), .clk(cl), .ld(In_out_prime));  // open: clr

  // Other names for the same wires on the sheet: IO_dat[7:0] = IO_output; rd_wr_prime = In_out_prime

  // Notes on the sheet:
  //   reset: pull=down
  //   Things to work with IO IN/OUT
  //   Cdm-8
  //   memory-mapped I/O
  //   read-1
  //   write-0
  //   instr memory
  //   data memory
  //   contents of rom_1 (hex, n*v repeats v):
  //   cd af d6 45 d6 16 d3 fd d2 1 ae d3 f9 d2 1 ae d6 16 d6 3a ee 10 d2 ee ba d6 55 d3 fa ae d3 ef bf f
  //   e0 2a d6 45 ee 16 ee 34 d3 ff d2 1 ae d3 ff d2 0 ae d3 fd d2 0 ae d7 d6 66 d2 fb ab d3 fd d2 1 ae d7
  //   d3 fc d2 1 ae d3 fc d2 0 ae d3 fd d2 2 ae d7 c2 d1 e6 b5 d3 ea bf 83 b4 4c d2 ec ba 58 a4 c6 d7 d1
  //   e7 b5 d3 eb bf b4 43 d2 fe ab d3 ed bf d7
endmodule

module eat_apple (
  input  [3:0] head_x,
  input  [3:0] apple_x,
  input  [3:0] head_y,
  input  [3:0] apple_y,
  output is_eat_apple
);

  wire or_1_out;
  wire [3:0] xor_1_out, xor_2_out;

  assign xor_1_out = head_x ^ apple_x;  // XOR_Gate xor_1, 4 bits wide
  assign xor_2_out = head_y ^ apple_y;  // XOR_Gate xor_2, 4 bits wide
  or or_1 (or_1_out, xor_1_out[0], xor_1_out[1], xor_1_out[2], xor_1_out[3], xor_2_out[0], xor_2_out[1], xor_2_out[2], xor_2_out[3]);
  not not_1 (is_eat_apple, or_1_out);

  // Notes on the sheet:
  //   Checking whether the snake has eaten an apple
endmodule

module change_coords (
  input  update,
  input  [1:0] Direction,
  input  [3:0] X,
  input  [3:0] Y,
  output [3:0] new_x,
  output [3:0] new_y
);

  wire [3:0] adder_1_out, adder_2_out, multiplexer_1_out, multiplexer_2_out, multiplexer_3_out,
       multiplexer_4_out;

  Multiplexer #(.width(4)) multiplexer_1 (
    .in0(4'b1111), .in1(4'b0001), .out(multiplexer_1_out), .sel(Direction[0]));  // open: en
  Multiplexer #(.width(4)) multiplexer_2 (
    .in0(4'b1111), .in1(4'b0001), .out(multiplexer_2_out), .sel(Direction[0]));  // open: en
  Multiplexer #(.width(4)) multiplexer_3 (
    .in0(X), .in1(adder_1_out), .out(multiplexer_3_out), .sel(Direction[1]));  // open: en
  Adder #(.width(4)) adder_1 (.a(multiplexer_1_out), .b(X), .out(adder_1_out));  // open: cin, cout
  Adder #(.width(4)) adder_2 (.a(multiplexer_2_out), .b(Y), .out(adder_2_out));  // open: cin, cout
  Multiplexer #(.width(4)) multiplexer_4 (
    .in0(adder_2_out), .in1(Y), .out(multiplexer_4_out), .sel(Direction[1]));  // open: en
  Register #(.width(4)) register_1 (.D(multiplexer_3_out), .Q(new_x), .clk(update));  // open: en, clr
  Register #(.width(4)) register_2 (.D(multiplexer_4_out), .Q(new_y), .clk(update));  // open: en, clr

  // Other names for the same wires on the sheet: Dir_0 = Direction[0]; Dir_1 = Direction[1]

  // Notes on the sheet:
  //   new_x: pull=down
  //   Changing coordinates according to the direction
endmodule

module score (
  input  apple_is_eaten,
  output [3:0] third_digit,
  output [3:0] second_digit,
  output [3:0] first_digit
);

  wire comparator_1_gt, comparator_2_gt, comparator_3_gt;
  wire [3:0] adder_1_out, adder_2_out, adder_3_out, register_1_q, register_2_q, register_3_q;

  Adder #(.width(4)) adder_1 (.a(register_1_q), .b(4'b0001), .out(adder_1_out));  // open: cin, cout
  Register #(.width(4)) register_1 (
    .D(adder_1_out), .Q(register_1_q), .clk(comparator_2_gt), .clr(comparator_1_gt));  // open: en
  Adder #(.width(4)) adder_2 (.a(register_2_q), .b(4'b0001), .out(adder_2_out));  // open: cin, cout
  Adder #(.width(4)) adder_3 (.a(register_3_q), .b(4'b0001), .out(adder_3_out));  // open: cin, cout
  Register #(.width(4)) register_2 (
    .D(adder_2_out), .Q(register_2_q), .clk(comparator_3_gt), .clr(comparator_2_gt));  // open: en
  Register #(.width(4)) register_3 (
    .D(adder_3_out), .Q(register_3_q), .clk(apple_is_eaten), .clr(comparator_3_gt));  // open: en
  Multiplexer #(.width(4)) multiplexer_1 (
    .in0(register_1_q), .in1(4'b0000), .out(third_digit), .sel(comparator_1_gt));  // open: en
  Comparator #(.width(4), .mode("unsigned")) comparator_1 (
    .a(register_1_q), .b(4'b1001), .gt(comparator_1_gt));  // open: eq, lt
  Multiplexer #(.width(4)) multiplexer_2 (
    .in0(register_2_q), .in1(4'b0000), .out(second_digit), .sel(comparator_2_gt));  // open: en
  Comparator #(.width(4), .mode("unsigned")) comparator_2 (
    .a(register_2_q), .b(4'b1001), .gt(comparator_2_gt));  // open: eq, lt
  Multiplexer #(.width(4)) multiplexer_3 (
    .in0(register_3_q), .in1(4'b0000), .out(first_digit), .sel(comparator_3_gt));  // open: en
  Comparator #(.width(4), .mode("unsigned")) comparator_3 (
    .a(register_3_q), .b(4'b1001), .gt(comparator_3_gt));  // open: eq, lt

  // Other names for the same wires on the sheet: is_eaten = apple_is_eaten
endmodule

module food_generating (
  input  clock,
  input  new_apple,
  input  Err,
  output [3:0] food_x,
  output [3:0] food_y,
  output stop
);

  wire _1_2_out, _1_out, _2_out, and_1_out, and_2_out, and_3_out, flag, not_1_out, not_2_out, not_3_out,
       not_4_out, not_5_out, not_6_out, or_1_out, or_2_out;
  wire [1:0] Counter;
  wire [3:0] food_x_t, food_y_t;

  Counter #(.width(6), .max('h3f)) counter_1 (.clk(Err));  // open: load, D, count, Q, carry, clr
  Counter #(.width(2), .max('h3)) counter_2 (.Q(Counter), .clk(clock), .clr(not_1_out));  // open: load, D, count, carry
  not not_1 (not_1_out, new_apple);
  or or_1 (or_1_out, new_apple, Err);
  and _1 (_1_out, Counter[0], ~Counter[1]);  // AND_Gate
  not not_2 (not_2_out, flag);
  and and_1 (and_1_out, or_1_out, not_2_out, _1_out);
  and _2 (_2_out, ~Counter[0], Counter[1]);  // AND_Gate
  not not_3 (not_3_out, Err);
  and _1_2 (_1_2_out, Counter[0], ~Counter[1]);  // AND_Gate
  not not_4 (not_4_out, flag);
  and and_2 (and_2_out, _2_out, not_3_out, stop);
  not not_5 (not_5_out, new_apple);
  not not_6 (not_6_out, new_apple);
  Random #(.width(4), .seed(5)) random_1 (.clk(clock), .out(food_x_t));  // open: next, clr
  Random #(.width(4)) random_2 (.clk(clock), .out(food_y_t));  // open: next, clr
  and and_3 (and_3_out, _1_2_out, not_4_out);
  or or_2 (or_2_out, and_2_out, not_5_out);
  Register #(.width(1)) register_1 (.D(1'b1), .Q(flag), .clk(and_2_out), .clr(not_6_out));  // open: en
  Register #(.width(4)) register_2 (.D(food_x_t), .Q(food_x), .clk(and_1_out));  // open: en, clr
  Register #(.width(4)) register_3 (.D(food_y_t), .Q(food_y), .clk(and_1_out));  // open: en, clr
  Register #(.width(1)) register_4 (.D(1'b1), .Q(stop), .clk(and_3_out), .clr(or_2_out));  // open: en

  // Notes on the sheet:
  //   Circuit to generate new apple coordinates
endmodule

module screen_chooser (
  input  [2:0] screen_select,
  input  [15:0] in_2,
  input  [15:0] in_3,
  input  [15:0] in_4,
  input  [15:0] in_5,
  input  [15:0] in_6,
  input  [15:0] in_7,
  input  [15:0] in_8,
  input  [15:0] in_9,
  input  [15:0] in_10,
  input  [15:0] in_11,
  input  [15:0] in_12,
  input  [15:0] in_13,
  input  [15:0] in_14,
  input  [15:0] in_15,
  input  [15:0] in_16,
  input  [15:0] in_17,
  output [31:0] line_1,
  output [31:0] line_2,
  output [31:0] line_3,
  output [31:0] line_4,
  output [31:0] line_5,
  output [31:0] line_6,
  output [31:0] line_7,
  output [31:0] line_8,
  output [31:0] line_9,
  output [31:0] line_10,
  output [31:0] line_11,
  output [31:0] line_12,
  output [31:0] line_13,
  output [31:0] line_14,
  output [31:0] line_15,
  output [31:0] line_16,
  output [31:0] line_17,
  output [31:0] line_18,
  output [31:0] line_19,
  output [31:0] line_20,
  output [31:0] line_21,
  output [31:0] line_22,
  output [31:0] line_23,
  output [31:0] line_24,
  output [31:0] line_25,
  output [31:0] line_26,
  output [31:0] line_27,
  output [31:0] line_28,
  output [31:0] line_29,
  output [31:0] line_30,
  output [31:0] line_31,
  output [31:0] line_32
);

  wire [31:0] game_1, game_2, game_3, game_4, game_5, game_6, game_7, game_8, game_9, game_10, game_11,
       game_12, game_13, game_14, game_15, game_16, game_over_1, game_over_2, game_over_3, game_over_4,
       game_over_5, game_over_6, game_over_10, game_over_11, game_over_12, game_over_13, game_over_14,
       game_over_15, game_over_16, game_over_17, game_over_18, game_over_19, game_over_20, game_over_21,
       game_over_22, game_over_23, game_over_24, game_over_25, game_over_26, game_over_27, game_over_28,
       game_over_29, game_over_30, game_over_31, game_over_32, game_over__7, game_over__8, game_over__9,
       start_1, start_2, start_3, start_4, start_5, start_6, start_7, start_8, start_9, start_10, start_11,
       start_12, start_13, start_14, start_15, start_16, start_17, start_18, start_19, start_20, start_21,
       start_22, start_23, start_24, start_25, start_26, start_27, start_28, start_29, start_30, start_31,
       start_32;

  _16_to_32 u_16_to_32_1 (.in_1(in_2), .out_2(game_1));
  _16_to_32 u_16_to_32_2 (.in_1(in_3), .out_2(game_2));
  _16_to_32 u_16_to_32_3 (.in_1(in_4), .out_2(game_3));
  _16_to_32 u_16_to_32_4 (.in_1(in_5), .out_2(game_4));
  _16_to_32 u_16_to_32_5 (.in_1(in_6), .out_2(game_5));
  _16_to_32 u_16_to_32_6 (.in_1(in_7), .out_2(game_6));
  _16_to_32 u_16_to_32_7 (.in_1(in_8), .out_2(game_7));
  _16_to_32 u_16_to_32_8 (.in_1(in_9), .out_2(game_8));
  _16_to_32 u_16_to_32_9 (.in_1(in_10), .out_2(game_9));
  _16_to_32 u_16_to_32_10 (.in_1(in_11), .out_2(game_10));
  _16_to_32 u_16_to_32_11 (.in_1(in_12), .out_2(game_11));
  _16_to_32 u_16_to_32_12 (.in_1(in_13), .out_2(game_12));
  _16_to_32 u_16_to_32_13 (.in_1(in_14), .out_2(game_13));
  _16_to_32 u_16_to_32_14 (.in_1(in_15), .out_2(game_14));
  _16_to_32 u_16_to_32_15 (.in_1(in_16), .out_2(game_15));
  _16_to_32 u_16_to_32_16 (.in_1(in_17), .out_2(game_16));
  game_over_screen game_over_screen_1 (
    .out_1(game_over_1), .out_2(game_over_17), .out_3(game_over_2), .out_4(game_over_18),
    .out_5(game_over_3), .out_6(game_over_19), .out_7(game_over_4), .out_8(game_over_20),
    .out_9(game_over_5), .out_10(game_over_21), .out_11(game_over_6), .out_12(game_over_22),
    .out_13(game_over__7), .out_14(game_over_23), .out_15(game_over__8), .out_16(game_over_24),
    .out_17(game_over__9), .out_18(game_over_25), .out_19(game_over_10), .out_20(game_over_26),
    .out_21(game_over_11), .out_22(game_over_27), .out_23(game_over_12), .out_24(game_over_28),
    .out_25(game_over_13), .out_26(game_over_29), .out_27(game_over_14), .out_28(game_over_30),
    .out_29(game_over_15), .out_30(game_over_31), .out_31(game_over_16), .out_32(game_over_32));
  start_screen start_screen_1 (
    .out_1(start_1), .out_3(start_2), .out_5(start_3), .out_7(start_4), .out_9(start_5), .out_11(start_6),
    .out_13(start_7), .out_15(start_8), .out_17(start_9), .out_19(start_10), .out_21(start_11),
    .out_23(start_12), .out_25(start_13), .out_27(start_14), .out_29(start_15), .out_31(start_16),
    .out_2(start_17), .out_4(start_18), .out_6(start_19), .out_8(start_20), .out_10(start_21),
    .out_12(start_22), .out_14(start_23), .out_16(start_24), .out_18(start_25), .out_20(start_26),
    .out_22(start_27), .out_24(start_28), .out_26(start_29), .out_28(start_30), .out_30(start_31),
    .out_32(start_32));
  Multiplexer #(.select(3), .width(32)) multiplexer_1 (
    .in0(start_1), .in1(game_1), .in2(game_over_1), .out(line_1), .sel(screen_select));  // open: in3, in4, in5, in6, in7, en
  Multiplexer #(.select(3), .width(32)) multiplexer_2 (
    .in0(start_5), .in1(game_3), .in2(game_over_5), .out(line_5), .sel(screen_select));  // open: in3, in4, in5, in6, in7, en
  Multiplexer #(.select(3), .width(32)) multiplexer_3 (
    .in0(start_9), .in1(game_5), .in2(game_over__9), .out(line_9), .sel(screen_select));  // open: in3, in4, in5, in6, in7, en
  Multiplexer #(.select(3), .width(32)) multiplexer_4 (
    .in0(start_13), .in1(game_7), .in2(game_over_13), .out(line_13), .sel(screen_select));  // open: in3, in4, in5, in6, in7, en
  Multiplexer #(.select(3), .width(32)) multiplexer_5 (
    .in0(start_17), .in1(game_9), .in2(game_over_17), .out(line_17), .sel(screen_select));  // open: in3, in4, in5, in6, in7, en
  Multiplexer #(.select(3), .width(32)) multiplexer_6 (
    .in0(start_21), .in1(game_11), .in2(game_over_21), .out(line_21), .sel(screen_select));  // open: in3, in4, in5, in6, in7, en
  Multiplexer #(.select(3), .width(32)) multiplexer_7 (
    .in0(start_25), .in1(game_13), .in2(game_over_25), .out(line_25), .sel(screen_select));  // open: in3, in4, in5, in6, in7, en
  Multiplexer #(.select(3), .width(32)) multiplexer_8 (
    .in0(start_29), .in1(game_15), .in2(game_over_29), .out(line_29), .sel(screen_select));  // open: in3, in4, in5, in6, in7, en
  Multiplexer #(.select(3), .width(32)) multiplexer_9 (
    .in0(start_2), .in1(game_1), .in2(game_over_2), .out(line_2), .sel(screen_select));  // open: in3, in4, in5, in6, in7, en
  Multiplexer #(.select(3), .width(32)) multiplexer_10 (
    .in0(start_6), .in1(game_3), .in2(game_over_6), .out(line_6), .sel(screen_select));  // open: in3, in4, in5, in6, in7, en
  Multiplexer #(.select(3), .width(32)) multiplexer_11 (
    .in0(start_10), .in1(game_5), .in2(game_over_10), .out(line_10), .sel(screen_select));  // open: in3, in4, in5, in6, in7, en
  Multiplexer #(.select(3), .width(32)) multiplexer_12 (
    .in0(start_14), .in1(game_7), .in2(game_over_14), .out(line_14), .sel(screen_select));  // open: in3, in4, in5, in6, in7, en
  Multiplexer #(.select(3), .width(32)) multiplexer_13 (
    .in0(start_18), .in1(game_9), .in2(game_over_18), .out(line_18), .sel(screen_select));  // open: in3, in4, in5, in6, in7, en
  Multiplexer #(.select(3), .width(32)) multiplexer_14 (
    .in0(start_22), .in1(game_11), .in2(game_over_22), .out(line_22), .sel(screen_select));  // open: in3, in4, in5, in6, in7, en
  Multiplexer #(.select(3), .width(32)) multiplexer_15 (
    .in0(start_26), .in1(game_13), .in2(game_over_26), .out(line_26), .sel(screen_select));  // open: in3, in4, in5, in6, in7, en
  Multiplexer #(.select(3), .width(32)) multiplexer_16 (
    .in0(start_30), .in1(game_15), .in2(game_over_30), .out(line_30), .sel(screen_select));  // open: in3, in4, in5, in6, in7, en
  Multiplexer #(.select(3), .width(32)) multiplexer_17 (
    .in0(start_3), .in1(game_2), .in2(game_over_3), .out(line_3), .sel(screen_select));  // open: in3, in4, in5, in6, in7, en
  Multiplexer #(.select(3), .width(32)) multiplexer_18 (
    .in0(start_7), .in1(game_4), .in2(game_over__7), .out(line_7), .sel(screen_select));  // open: in3, in4, in5, in6, in7, en
  Multiplexer #(.select(3), .width(32)) multiplexer_19 (
    .in0(start_11), .in1(game_6), .in2(game_over_11), .out(line_11), .sel(screen_select));  // open: in3, in4, in5, in6, in7, en
  Multiplexer #(.select(3), .width(32)) multiplexer_20 (
    .in0(start_15), .in1(game_8), .in2(game_over_15), .out(line_15), .sel(screen_select));  // open: in3, in4, in5, in6, in7, en
  Multiplexer #(.select(3), .width(32)) multiplexer_21 (
    .in0(start_19), .in1(game_10), .in2(game_over_19), .out(line_19), .sel(screen_select));  // open: in3, in4, in5, in6, in7, en
  Multiplexer #(.select(3), .width(32)) multiplexer_22 (
    .in0(start_23), .in1(game_12), .in2(game_over_23), .out(line_23), .sel(screen_select));  // open: in3, in4, in5, in6, in7, en
  Multiplexer #(.select(3), .width(32)) multiplexer_23 (
    .in0(start_27), .in1(game_14), .in2(game_over_27), .out(line_27), .sel(screen_select));  // open: in3, in4, in5, in6, in7, en
  Multiplexer #(.select(3), .width(32)) multiplexer_24 (
    .in0(start_31), .in1(game_16), .in2(game_over_31), .out(line_31), .sel(screen_select));  // open: in3, in4, in5, in6, in7, en
  Multiplexer #(.select(3), .width(32)) multiplexer_25 (
    .in0(start_4), .in1(game_2), .in2(game_over_4), .out(line_4), .sel(screen_select));  // open: in3, in4, in5, in6, in7, en
  Multiplexer #(.select(3), .width(32)) multiplexer_26 (
    .in0(start_8), .in1(game_4), .in2(game_over__8), .out(line_8), .sel(screen_select));  // open: in3, in4, in5, in6, in7, en
  Multiplexer #(.select(3), .width(32)) multiplexer_27 (
    .in0(start_12), .in1(game_6), .in2(game_over_12), .out(line_12), .sel(screen_select));  // open: in3, in4, in5, in6, in7, en
  Multiplexer #(.select(3), .width(32)) multiplexer_28 (
    .in0(start_16), .in1(game_8), .in2(game_over_16), .out(line_16), .sel(screen_select));  // open: in3, in4, in5, in6, in7, en
  Multiplexer #(.select(3), .width(32)) multiplexer_29 (
    .in0(start_20), .in1(game_10), .in2(game_over_20), .out(line_20), .sel(screen_select));  // open: in3, in4, in5, in6, in7, en
  Multiplexer #(.select(3), .width(32)) multiplexer_30 (
    .in0(start_24), .in1(game_12), .in2(game_over_24), .out(line_24), .sel(screen_select));  // open: in3, in4, in5, in6, in7, en
  Multiplexer #(.select(3), .width(32)) multiplexer_31 (
    .in0(start_28), .in1(game_14), .in2(game_over_28), .out(line_28), .sel(screen_select));  // open: in3, in4, in5, in6, in7, en
  Multiplexer #(.select(3), .width(32)) multiplexer_32 (
    .in0(start_32), .in1(game_16), .in2(game_over_32), .out(line_32), .sel(screen_select));  // open: in3, in4, in5, in6, in7, en

  // Notes on the sheet:
  //   Main game screen
  //   0 - start screen
  //   game over screen
  //   start screen
  //   1 - main game screen
  //   2 - game over screen
  //   1-4
  //   5-8
  //   9-12
  //   13-16
  //   17-20
  //   21-24
  //   25-28
  //   29-32
  //   Output screen
endmodule

module _16_to_32 (
  input  [15:0] in_1,
  output [31:0] out_2
);


  assign out_2 = {{2{in_1[15]}}, {2{in_1[14]}}, {2{in_1[13]}}, {2{in_1[12]}}, {2{in_1[11]}}, {2{in_1[10]}}, {2{in_1[9]}}, {2{in_1[8]}}, {2{in_1[7]}}, {2{in_1[6]}}, {2{in_1[5]}}, {2{in_1[4]}}, {2{in_1[3]}}, {2{in_1[2]}}, {2{in_1[1]}}, {2{in_1[0]}}};
endmodule

module _8_to_4 (
  input  [7:0] in_1,
  output [3:0] out_2
);


  assign out_2 = in_1[3:0];
endmodule

module _4_to_1 (
  input  [3:0] in_1,
  output out_2
);


  assign out_2 = in_1[0];
endmodule

module _4_to_2 (
  input  [3:0] in_1,
  output [1:0] out_2
);


  assign out_2 = in_1[1:0];
endmodule

module _8_to_1 (
  input  [7:0] in_1,
  output out_2
);


  assign out_2 = in_1[0];
endmodule

module _8__3 (
  input  [7:0] in_1,
  output [2:0] out_2
);


  assign out_2 = in_1[2:0];
endmodule

module start_screen (
  output [31:0] out_1,
  output [31:0] out_2,
  output [31:0] out_3,
  output [31:0] out_4,
  output [31:0] out_5,
  output [31:0] out_6,
  output [31:0] out_7,
  output [31:0] out_8,
  output [31:0] out_9,
  output [31:0] out_10,
  output [31:0] out_11,
  output [31:0] out_12,
  output [31:0] out_13,
  output [31:0] out_14,
  output [31:0] out_15,
  output [31:0] out_16,
  output [31:0] out_17,
  output [31:0] out_18,
  output [31:0] out_19,
  output [31:0] out_20,
  output [31:0] out_21,
  output [31:0] out_22,
  output [31:0] out_23,
  output [31:0] out_24,
  output [31:0] out_25,
  output [31:0] out_26,
  output [31:0] out_27,
  output [31:0] out_28,
  output [31:0] out_29,
  output [31:0] out_30,
  output [31:0] out_31,
  output [31:0] out_32
);

  DotMatrix #(.inputtype("row"), .matrixcols(32), .matrixrows(32)) dotmatrix_1 (
    .row0({32{1'b0}}), .row1({32{1'b0}}), .row2(32'h3d09c8be), .row3(32'h418a2920), .row4(32'h414a2a20),
    .row5(32'h792bec3c), .row6(32'h51a2a20), .row7(32'h50a2920), .row8(32'h790a28be), .row9({32{1'b0}}),
    .row10({32{1'b0}}), .row11(32'h4f0), .row12(32'h2807f8), .row13(32'h30031c), .row14(32'h20000c),
    .row15(32'h70000c), .row16(32'hf83f1c), .row17(32'hf87ff8), .row18(32'hf8e1f0), .row19(32'h71c000),
    .row20(32'h19f00), .row21(32'ha01ff80), .row22(32'hc00f1c0), .row23(32'h80000e0), .row24(32'h1c01f070),
    .row25(32'h3e03f830), .row26(32'h3e03dc30), .row27(32'h3e038e70), .row28(32'h1c0007e0), .row29(32'h180),
    .row30({32{1'b0}}), .row31({32{1'b0}}));

  assign out_1 = {32{1'b0}};
  assign out_2 = 32'hf83f1c;
  assign out_3 = {32{1'b0}};
  assign out_4 = 32'hf87ff8;
  assign out_5 = 32'h3d09c8be;
  assign out_6 = 32'hf8e1f0;
  assign out_7 = 32'h418a2920;
  assign out_8 = 32'h71c000;
  assign out_9 = 32'h414a2a20;
  assign out_10 = 32'h19f00;
  assign out_11 = 32'h792bec3c;
  assign out_12 = 32'ha01ff80;
  assign out_13 = 32'h51a2a20;
  assign out_14 = 32'hc00f1c0;
  assign out_15 = 32'h50a2920;
  assign out_16 = 32'h80000e0;
  assign out_17 = 32'h790a28be;
  assign out_18 = 32'h1c01f070;
  assign out_19 = {32{1'b0}};
  assign out_20 = 32'h3e03f830;
  assign out_21 = {32{1'b0}};
  assign out_22 = 32'h3e03dc30;
  assign out_23 = 32'h4f0;
  assign out_24 = 32'h3e038e70;
  assign out_25 = 32'h2807f8;
  assign out_26 = 32'h1c0007e0;
  assign out_27 = 32'h30031c;
  assign out_28 = 32'h180;
  assign out_29 = 32'h20000c;
  assign out_30 = {32{1'b0}};
  assign out_31 = 32'h70000c;
  assign out_32 = {32{1'b0}};
endmodule

module game_over_screen (
  output [31:0] out_1,
  output [31:0] out_2,
  output [31:0] out_3,
  output [31:0] out_4,
  output [31:0] out_5,
  output [31:0] out_6,
  output [31:0] out_7,
  output [31:0] out_8,
  output [31:0] out_9,
  output [31:0] out_10,
  output [31:0] out_11,
  output [31:0] out_12,
  output [31:0] out_13,
  output [31:0] out_14,
  output [31:0] out_15,
  output [31:0] out_16,
  output [31:0] out_17,
  output [31:0] out_18,
  output [31:0] out_19,
  output [31:0] out_20,
  output [31:0] out_21,
  output [31:0] out_22,
  output [31:0] out_23,
  output [31:0] out_24,
  output [31:0] out_25,
  output [31:0] out_26,
  output [31:0] out_27,
  output [31:0] out_28,
  output [31:0] out_29,
  output [31:0] out_30,
  output [31:0] out_31,
  output [31:0] out_32
);

  DotMatrix #(.inputtype("row"), .matrixcols(32), .matrixrows(32)) dotmatrix_1 (
    .row0({32{1'b0}}), .row1({32{1'b0}}), .row2({32{1'b0}}), .row3({32{1'b0}}), .row4({32{1'b0}}),
    .row5({32{1'b0}}), .row6(32'h3e3e637e), .row7(32'h63637760), .row8(32'h60637f60), .row9(32'h60636b60),
    .row10(32'h677f637c), .row11(32'h63636360), .row12(32'h23636360), .row13(32'h1d63637e),
    .row14({32{1'b0}}), .row15({32{1'b0}}), .row16(32'h3e637efc), .row17(32'h636360c6), .row18(32'h636360c6),
    .row19(32'h636360fc), .row20(32'h63637cc6), .row21(32'h633660c6), .row22(32'h631c60c6),
    .row23(32'h3e087ec6), .row24({32{1'b0}}), .row25({32{1'b0}}), .row26({32{1'b0}}), .row27({32{1'b0}}),
    .row28({32{1'b0}}), .row29({32{1'b0}}), .row30({32{1'b0}}), .row31({32{1'b0}}));

  assign out_1 = {32{1'b0}};
  assign out_2 = 32'h3e637efc;
  assign out_3 = {32{1'b0}};
  assign out_4 = 32'h636360c6;
  assign out_5 = {32{1'b0}};
  assign out_6 = 32'h636360c6;
  assign out_7 = {32{1'b0}};
  assign out_8 = 32'h636360fc;
  assign out_9 = {32{1'b0}};
  assign out_10 = 32'h63637cc6;
  assign out_11 = {32{1'b0}};
  assign out_12 = 32'h633660c6;
  assign out_13 = 32'h3e3e637e;
  assign out_14 = 32'h631c60c6;
  assign out_15 = 32'h63637760;
  assign out_16 = 32'h3e087ec6;
  assign out_17 = 32'h60637f60;
  assign out_18 = {32{1'b0}};
  assign out_19 = 32'h60636b60;
  assign out_20 = {32{1'b0}};
  assign out_21 = 32'h677f637c;
  assign out_22 = {32{1'b0}};
  assign out_23 = 32'h63636360;
  assign out_24 = {32{1'b0}};
  assign out_25 = 32'h23636360;
  assign out_26 = {32{1'b0}};
  assign out_27 = 32'h1d63637e;
  assign out_28 = {32{1'b0}};
  assign out_29 = {32{1'b0}};
  assign out_30 = {32{1'b0}};
  assign out_31 = {32{1'b0}};
  assign out_32 = {32{1'b0}};
endmodule
